// Logisim project MusicPayer.circ as structural Verilog: 1 circuit, main circuit main
module main (
  input  ON_OFF,
  input  in_2
);

  wire and_1_out, and_2_out, and_3_out, and_4_out, and_5_out, and_6_out, and_7_out, and_8_out, and_9_out,
       and_10_out, and_11_out, and_12_out, and_13_out, and_14_out, and_15_out, and_16_out, and_17_out,
       and_18_out, and_19_out, and_20_out, and_21_out, and_22_out, and_23_out, and_24_out, and_25_out,
       and_26_out, and_27_out, and_28_out, and_29_out, and_30_out, and_31_out, and_32_out, and_33_out,
       and_34_out, and_35_out, and_36_out, and_37_out, and_38_out, and_39_out, and_40_out, and_41_out,
       and_42_out, and_43_out, and_44_out, and_45_out, and_46_out, and_47_out, and_48_out, and_50_out,
       and_51_out, and_55_out, and_56_out, and_60_out, and_61_out, d_ff_1_q, d_ff_2_q, d_ff_3_q, d_ff_4_q,
       d_ff_5_q, d_ff_6_q, d_ff_7_q, d_ff_8_q, d_ff_9_q, d_ff_10_q, j_k_ff_1_q, j_k_ff_1_qn, j_k_ff_2_q,
       j_k_ff_2_qn, j_k_ff_3_q, j_k_ff_3_qn, j_k_ff_4_q, j_k_ff_4_qn, j_k_ff_5_q, j_k_ff_5_qn, j_k_ff_6_q,
       j_k_ff_6_qn, j_k_ff_7_q, j_k_ff_7_qn, j_k_ff_8_q, j_k_ff_9_q, NextTrack_out, not_1_out, not_2_out,
       not_3_out, not_4_out, not_5_out, not_6_out, not_7_out, not_8_out, not_9_out, not_10_out, not_11_out,
       not_12_out, or_1_out, or_2_out, or_3_out, or_4_out, or_5_out, or_6_out, or_7_out, or_8_out, or_9_out,
       or_10_out, or_11_out, or_12_out, or_13_out, or_14_out, or_15_out, or_16_out, or_17_out, or_18_out,
       or_19_out, or_20_out, or_21_out, or_22_out, PAUSE_out, PLAY_out, PreviousTrack_out, s_r_ff_1_q,
       VolDOWN_out, VolUP_out, xnor_1_out;
  wire [3:0] and_49_out, and_57_out;

  Button PLAY (.out(PLAY_out));
  Button PAUSE (.out(PAUSE_out));
  Button VolUP (.out(VolUP_out));
  Button VolDOWN (.out(VolDOWN_out));
  Button NextTrack (.out(NextTrack_out));
  Button PreviousTrack (.out(PreviousTrack_out));
  S_R_Flip_Flop s_r_ff_1 (.Q(s_r_ff_1_q), .reset(NextTrack_out), .preset(and_1_out));  // open: S, R, clk, Qn
  and and_1 (and_1_out, PreviousTrack_out, ON_OFF);
  or or_1 (or_1_out, and_1_out, NextTrack_out);
  not not_1 (not_1_out, s_r_ff_1_q);
  not not_2 (not_2_out, or_1_out);
  and and_2 (and_2_out, d_ff_1_q, PAUSE_out);
  and and_3 (and_3_out, ON_OFF, VolUP_out);
  and and_4 (and_4_out, ON_OFF, VolDOWN_out);
  D_Flip_Flop d_ff_1 (.D(PLAY_out), .clk(PLAY_out), .Q(d_ff_1_q));  // open: Qn, preset, reset
  not not_3 (not_3_out, d_ff_2_q);
  or or_2 (or_2_out, and_45_out, and_37_out);
  J_K_Flip_Flop j_k_ff_1 (
    .J(or_3_out), .K(and_2_out), .clk(or_3_out), .Q(j_k_ff_1_q), .Qn(j_k_ff_1_qn), .reset(not_4_out));  // open: preset
  or or_3 (or_3_out, PLAY_out, and_2_out);
  D_Flip_Flop d_ff_2 (.Q(d_ff_2_q), .preset(and_3_out), .reset(and_4_out));  // open: D, clk, Qn
  not not_4 (not_4_out, ON_OFF);
  and and_5 (and_5_out, d_ff_4_q, not_3_out);
  and and_6 (and_6_out, d_ff_2_q, d_ff_2_q);
  and and_7 (and_7_out, d_ff_5_q, not_3_out);
  and and_8 (and_8_out, d_ff_2_q, d_ff_3_q);
  and and_9 (and_9_out, d_ff_6_q, not_3_out);
  and and_10 (and_10_out, d_ff_2_q, d_ff_4_q);
  and and_11 (and_11_out, d_ff_7_q, not_3_out);
  and and_12 (and_12_out, d_ff_2_q, d_ff_5_q);
  and and_13 (and_13_out, d_ff_8_q, not_3_out);
  and and_14 (and_14_out, d_ff_2_q, d_ff_6_q);
  and and_15 (and_15_out, d_ff_9_q, not_3_out);
  and and_16 (and_16_out, d_ff_2_q, d_ff_7_q);
  and and_17 (and_17_out, d_ff_10_q, not_3_out);
  and and_18 (and_18_out, d_ff_2_q, d_ff_8_q);
  and and_19 (and_19_out, in_2, not_3_out);
  and and_20 (and_20_out, d_ff_2_q, d_ff_9_q);
  or or_4 (or_4_out, and_61_out, and_60_out);
  J_K_Flip_Flop j_k_ff_2 (
    .J(ON_OFF), .K(ON_OFF), .clk(not_2_out), .Q(j_k_ff_2_q), .Qn(j_k_ff_2_qn), .preset(or_4_out),
    .reset(and_37_out));
  and and_21 (and_21_out, ON_OFF, j_k_ff_1_q);
  and and_22 (and_22_out, j_k_ff_1_qn, ON_OFF);
  xnor xnor_1 (xnor_1_out, and_3_out, and_4_out);
  or or_5 (or_5_out, and_5_out, and_6_out);
  or or_6 (or_6_out, and_7_out, and_8_out);
  or or_7 (or_7_out, and_9_out, and_10_out);
  or or_8 (or_8_out, and_11_out, and_12_out);
  or or_9 (or_9_out, and_13_out, and_14_out);
  or or_10 (or_10_out, and_15_out, and_16_out);
  or or_11 (or_11_out, and_17_out, and_18_out);
  or or_12 (or_12_out, and_19_out, and_20_out);
  J_K_Flip_Flop j_k_ff_3 (
    .J(ON_OFF), .K(ON_OFF), .clk(or_2_out), .Q(j_k_ff_3_q), .Qn(j_k_ff_3_qn), .preset(and_61_out),
    .reset(and_46_out));
  D_Flip_Flop d_ff_3 (.D(or_5_out), .clk(xnor_1_out), .Q(d_ff_3_q));  // open: Qn, preset, reset
  D_Flip_Flop d_ff_4 (.D(or_6_out), .clk(xnor_1_out), .Q(d_ff_4_q));  // open: Qn, preset, reset
  D_Flip_Flop d_ff_5 (.D(or_7_out), .clk(xnor_1_out), .Q(d_ff_5_q));  // open: Qn, preset, reset
  D_Flip_Flop d_ff_6 (.D(or_8_out), .clk(xnor_1_out), .Q(d_ff_6_q));  // open: Qn, preset, reset
  D_Flip_Flop d_ff_7 (.D(or_9_out), .clk(xnor_1_out), .Q(d_ff_7_q));  // open: Qn, preset, reset
  D_Flip_Flop d_ff_8 (.D(or_10_out), .clk(xnor_1_out), .Q(d_ff_8_q));  // open: Qn, preset, reset
  D_Flip_Flop d_ff_9 (.D(or_11_out), .clk(xnor_1_out), .Q(d_ff_9_q));  // open: Qn, preset, reset
  D_Flip_Flop d_ff_10 (.D(or_12_out), .clk(xnor_1_out), .Q(d_ff_10_q));  // open: Qn, preset, reset
  and and_23 (and_23_out, not_1_out, j_k_ff_2_q);
  and and_24 (and_24_out, s_r_ff_1_q, j_k_ff_2_qn);
  LED PLAY_LED (.in(and_21_out));
  and and_25 (and_25_out, not_1_out, j_k_ff_3_q);
  and and_26 (and_26_out, s_r_ff_1_q, j_k_ff_3_qn);
  LED PAUSE_LED (.in(and_22_out));
  J_K_Flip_Flop j_k_ff_4 (
    .J(or_13_out), .K(or_13_out), .clk(not_2_out), .Q(j_k_ff_4_q), .Qn(j_k_ff_4_qn), .reset(or_14_out));  // open: preset
  or or_13 (or_13_out, and_23_out, and_24_out);
  or or_14 (or_14_out, and_37_out, and_45_out);
  and and_27 (and_27_out, d_ff_3_q, ON_OFF);
  and and_28 (and_28_out, d_ff_4_q, ON_OFF);
  LED led_1 (.in(and_27_out));
  LED led_2 (.in(and_28_out));
  J_K_Flip_Flop j_k_ff_5 (
    .J(or_15_out), .K(or_15_out), .clk(or_2_out), .Q(j_k_ff_5_q), .Qn(j_k_ff_5_qn), .reset(or_16_out));  // open: preset
  or or_15 (or_15_out, and_25_out, and_26_out);
  or or_16 (or_16_out, and_46_out, and_48_out);
  LedBar VOLUME (
    .led0(and_27_out), .led1(and_28_out), .led2(and_29_out), .led3(and_32_out), .led4(and_33_out),
    .led5(and_36_out), .led6(and_38_out), .led7(and_39_out));
  and and_29 (and_29_out, d_ff_5_q, ON_OFF);
  LED led_3 (.in(and_29_out));
  and and_30 (and_30_out, and_23_out, j_k_ff_4_q);
  and and_31 (and_31_out, and_24_out, j_k_ff_4_qn);
  and and_32 (and_32_out, d_ff_6_q, ON_OFF);
  and and_33 (and_33_out, d_ff_7_q, ON_OFF);
  LED led_4 (.in(and_32_out));
  LED led_5 (.in(and_33_out));
  and and_34 (and_34_out, and_25_out, j_k_ff_5_q);
  and and_35 (and_35_out, and_26_out, j_k_ff_5_qn);
  Hex_Digit_Display hex_digit_display_1 (.value(and_57_out));  // open: dp
  and and_36 (and_36_out, d_ff_8_q, ON_OFF);
  LED led_6 (.in(and_36_out));
  or or_17 (or_17_out, and_30_out, and_31_out);
  and and_37 (and_37_out, not_1_out, and_44_out);
  Hex_Digit_Display hex_digit_display_2 (.value(and_49_out));  // open: dp
  and and_38 (and_38_out, d_ff_9_q, ON_OFF);
  and and_39 (and_39_out, d_ff_10_q, ON_OFF);
  LED led_7 (.in(and_38_out));
  LED led_8 (.in(and_39_out));
  J_K_Flip_Flop j_k_ff_6 (
    .J(or_17_out), .K(or_17_out), .clk(not_2_out), .Q(j_k_ff_6_q), .Qn(j_k_ff_6_qn), .reset(or_18_out));  // open: preset
  or or_18 (or_18_out, and_37_out, and_45_out);
  J_K_Flip_Flop j_k_ff_7 (
    .J(or_19_out), .K(or_19_out), .clk(or_2_out), .Q(j_k_ff_7_q), .Qn(j_k_ff_7_qn), .reset(or_20_out));  // open: preset
  or or_19 (or_19_out, and_34_out, and_35_out);
  or or_20 (or_20_out, and_46_out, and_48_out);
  and and_40 (and_40_out, and_30_out, j_k_ff_6_q);
  and and_41 (and_41_out, and_31_out, j_k_ff_6_qn);
  and and_42 (and_42_out, and_34_out, j_k_ff_7_q);
  and and_43 (and_43_out, and_35_out, j_k_ff_7_qn);
  or or_21 (or_21_out, and_40_out, and_41_out);
  and and_44 (and_44_out, j_k_ff_8_q, j_k_ff_4_q);
  and and_45 (and_45_out, s_r_ff_1_q, and_50_out);
  and and_46 (and_46_out, not_1_out, and_47_out);
  J_K_Flip_Flop j_k_ff_8 (
    .J(or_21_out), .K(or_21_out), .clk(not_2_out), .Q(j_k_ff_8_q), .preset(and_61_out), .reset(and_37_out));  // open: Qn
  J_K_Flip_Flop j_k_ff_9 (
    .J(or_22_out), .K(or_22_out), .clk(or_2_out), .Q(j_k_ff_9_q), .preset(and_61_out), .reset(and_46_out));  // open: Qn
  or or_22 (or_22_out, and_42_out, and_43_out);
  and and_47 (and_47_out, j_k_ff_9_q, j_k_ff_5_q);
  and and_48 (and_48_out, s_r_ff_1_q, and_51_out);
  and and_49 (and_49_out[0], j_k_ff_2_q, ON_OFF);
  and and_50 (and_50_out, j_k_ff_2_q, j_k_ff_4_q, j_k_ff_6_q, j_k_ff_8_q);
  and and_51 (and_51_out, j_k_ff_9_q, j_k_ff_7_q, j_k_ff_5_q, j_k_ff_3_q);
  and and_52 (and_49_out[1], j_k_ff_4_q, ON_OFF);
  and and_53 (and_49_out[2], j_k_ff_6_q, ON_OFF);
  and and_54 (and_49_out[3], j_k_ff_8_q, ON_OFF);
  not not_5 (not_5_out, j_k_ff_2_q);
  not not_6 (not_6_out, j_k_ff_4_q);
  not not_7 (not_7_out, j_k_ff_6_q);
  not not_8 (not_8_out, j_k_ff_8_q);
  not not_9 (not_9_out, j_k_ff_3_q);
  not not_10 (not_10_out, j_k_ff_5_q);
  not not_11 (not_11_out, j_k_ff_7_q);
  not not_12 (not_12_out, j_k_ff_9_q);
  and and_55 (and_55_out, not_5_out, not_6_out, not_7_out, not_8_out, not_9_out, not_10_out, not_11_out, not_12_out);
  and and_56 (and_56_out, not_5_out, not_6_out, not_7_out, not_8_out, not_9_out, not_10_out, not_11_out, not_12_out);
  and and_57 (and_57_out[0], j_k_ff_3_q, ON_OFF);
  and and_58 (and_57_out[1], j_k_ff_5_q, ON_OFF);
  and and_59 (and_57_out[2], j_k_ff_7_q, ON_OFF);
  and and_60 (and_60_out, and_55_out, ON_OFF, ON_OFF, not_1_out);
  and and_61 (and_61_out, and_56_out, ON_OFF, ON_OFF, s_r_ff_1_q);
  and and_62 (and_57_out[3], j_k_ff_9_q, ON_OFF);
endmodule
